# Fritzing sketch Right_Hand (saved by Fritzing 0.9.10b)
breadboards: 1

parts:
  元件9 = Arduino Leonardo (Rev3b)
  元件10 = 9-DOF Absolute Orientation IMU Fusion Breakout - BNO055
  元件11 = Flora TCS34725 Color Sensor
  元件12 = OLED Monochrome 128x64 0.96 inch [part_number=326]
  元件13 = Adafruit TCA9548A
  元件8 = Flora TCS34725 Color Sensor

nets:
  N1: 元件9.D2/SDA, 元件9.SDA, 元件13.INPUTSDA
  N2: 元件9.D3_PWM/SCL, 元件9.SCL, 元件13.INPUTSCL
  3.3V: 元件9.3V3, 元件10.3.3V, 元件10.SCL_5V, 元件11.3.3V, 元件12.3.3V, 元件13.7SCL, 元件13.VCC, 元件8.3.3V
  GND: 元件9.GND, 元件10.GND, 元件11.GND, 元件12.GND, 元件13.GND, 元件8.GND
  N3: 元件9.A0, 元件13.A0
  N4: 元件9.A1, 元件13.A1
  N5: 元件9.A2, 元件13.A2
  N6: 元件10.SDA_5V, 元件13.7SDA
  N7: 元件11.SDA, 元件11.SDA_3V, 元件13.2SDA
  N8: 元件11.SCL, 元件13.2SCL
  N9: 元件12.MOSI_SDA, 元件13.5SDA
  N10: 元件12.SCLK_SCK, 元件13.5SCL
  N11: 元件13.1SDA, 元件8.SDA, 元件8.SDA_3V
  N12: 元件13.1SCL, 元件8.SCL, 元件8.SCL_3V

custom parts:
  9-DOF Absolute Orientation IMU Fusion Breakout - BNO055: A MEMS accelerometer, magnetometer and gyroscope on a single die with a high speed ARM Cortex-M0 based processor to digest all the sensor data, abstract the sensor fusion and real time requirements away, and spit out data you can use in quaternions, Euler angles or vectors.
  Flora TCS34725 Color Sensor: Your electronics can now see in dazzling color with this lovely color light sensor. We found the best color sensor on the market, the TCS34725, which has RGB and Clear light sensing elements. An IR blocking filter, integrated on-chip and localized to the color sensing photodiodes, minimizes the IR spectral component of the incoming light and allows color measurements to be made accurately. The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
  OLED Monochrome 128x64 0.96 inch: These displays are small, only about 1" diameter, but very readable due to the high contrast of an OLED display. This display is made of 128x64 individual white OLED pixels, each one is turned on or off by the controller chip. Because the display makes its own light, no backlight is required. This reduces the power required to run the OLED and is why the display has such high contrast; we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
  Adafruit TCA9548A: You just found the perfect I2C sensor, and you want to wire up two or three or more of them to your Arduino when you realize "Uh oh, this chip has a fixed I2C address, and from what I know about I2C, you cannot have two devices with the same address on the same SDA/SCL pins!" Are you out of luck? You would be, if you didn't have this ultra-cool TCA9548A 1-to-8 I2C multiplexer! Finally, a way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
